# Fritzing sketch wiring (saved by Fritzing 0.9.3b)

parts:
  Bauteil1 = Arduino Nano (Rev3.0)
  MOTOR1 = 28BYJ-48 Stepper Motor
  BREAKOUT1 = ULN2003A breakout board

nets:
  N1: Bauteil1.D3, BREAKOUT1.In_4
  N2: Bauteil1.D4, BREAKOUT1.In_3
  N3: Bauteil1.D5, BREAKOUT1.In_2
  N4: Bauteil1.D6, BREAKOUT1.In_1
  N5: Bauteil1.GND, BREAKOUT1.0V
  5V: Bauteil1.5V, BREAKOUT1.+5V
  N6: MOTOR1.RED, BREAKOUT1.RED_wire
  N7: MOTOR1.ORANGE, BREAKOUT1.ORANGE_wire
  N8: MOTOR1.YELLOW, BREAKOUT1.YELLOW_wire
  N9: MOTOR1.PINK, BREAKOUT1.PINK_wire
  N10: MOTOR1.BLUE, BREAKOUT1.BLUE_wire

custom parts:
  ULN2003A breakout board: ULN2003A 7-way Darlington Transistor Driver on breakoutboard
