# Fritzing sketch wiring_buttons (saved by Fritzing 0.9.6b)

parts:
  Bauteil1 = Arduino Nano (Rev3.0)
  S2 = Round Pushbutton [part_number=IN]
  S3 = Round Pushbutton [part_number=OUT]
  R1 = Rotary Potentiometer (Small) [maximum_resistance=100kΩ package=THT]

nets:
  N1: Bauteil1.GND, S2.leg1, S3.leg1, R1.leg2
  N2: Bauteil1.D7, S3.leg0
  N3: Bauteil1.D8, S2.leg0
  N4: Bauteil1.VIN, R1.leg1
  N5: Bauteil1.A0, R1.wiper
