# Fritzing sketch wiring_driver (saved by Fritzing 0.9.3b)

parts:
  Bauteil1 = Arduino Nano (Rev3.0)
  Pololu_A1 = Pololu A4988 [package=SO16]
  M1 = Stepper Motor - Bipolar
  Power_plug1 = Power plug

nets:
  N1: Bauteil1.GND, Pololu_A1.GND#8
  N2: Bauteil1.D3, Pololu_A1.DIR
  N3: Bauteil1.D4, Pololu_A1.SLEEP
  N4: Bauteil1.D5, Pololu_A1.STEP
  5V: Bauteil1.5V, Pololu_A1.RESET, Pololu_A1.VDD
  N5: Pololu_A1.1B, M1.D
  N6: Pololu_A1.1A, M1.B
  N7: Pololu_A1.2A, M1.C
  N8: Pololu_A1.2B, M1.A
  N9: Pololu_A1.GND#14, Power_plug1.GND
  N10: Pololu_A1.VMOT, Power_plug1.VCC
