# Fritzing sketch wiring_temperature (saved by Fritzing 0.9.3b)

parts:
  Bauteil1 = Arduino Nano (Rev3.0)
  DS1 = DS18B20 1-Wire Temperature Sensor [part_number=DS18B20]
  R1 = Resistor [tolerance=±5% resistance=4.7k package="2512 [SMD]"]

nets:
  GND: Bauteil1.GND, DS1.GND
  N1: Bauteil1.D2, DS1.DQ, R1.Pin_1
  N2: Bauteil1.5V, R1.Pin_0
